# Fritzing sketch Signal_Circuit (saved by Fritzing 0.9.3b)
circuit board: 10cm x 6cm
breadboards: 1

parts:
  U1 = RELAY [package=relay-jzc]
  U2 = RELAY [package=relay-jzc]
  U3 = RELAY [package=relay-jzc]
  U4 = RELAY [package=relay-jzc]
  D1 = Rectifier Diode [part_number=1N4001 package="Melf DO-213 AB [SMD]"]
  Q1 = NPN-Transistor [package="SOT-23 [SMD]"]
  D2 = Rectifier Diode [part_number=1N4001 package="Melf DO-213 AB [SMD]"]
  D3 = Rectifier Diode [part_number=1N4001 package="Melf DO-213 AB [SMD]"]
  D4 = Rectifier Diode [part_number=1N4001 package="Melf DO-213 AB [SMD]"]
  Q2 = NPN-Transistor [package="SOT-23 [SMD]"]
  Q3 = NPN-Transistor [package="SOT-23 [SMD]"]
  Q4 = NPN-Transistor [package="SOT-23 [SMD]"]
  R1 = Resistor [tolerance=±5% resistance=220 package=THT]
  R2 = Resistor [tolerance=±5% resistance=220 package=THT]
  R3 = Resistor [tolerance=±5% resistance=220 package=THT]
  R4 = Resistor [tolerance=±5% resistance=220 package=THT]
  D5 = Rectifier Diode [part_number=1N4001 package="Melf DO-213 AB [SMD]"]
  D6 = Rectifier Diode [part_number=1N4001 package="Melf DO-213 AB [SMD]"]
  D7 = Rectifier Diode [part_number=1N4001 package="Melf DO-213 AB [SMD]"]
  D8 = Rectifier Diode [part_number=1N4001 package="Melf DO-213 AB [SMD]"]
  LED1 = smd LED [color="Red (633nm)" package="0805 [SMD]"]
  Q5 = NPN-Transistor [package="SOT-23 [SMD]"]
  R5 = Resistor [tolerance=±5% resistance=220 package=THT]
  R6 = Resistor [tolerance=±5% resistance=220 package=THT]
  Q6 = NPN-Transistor [package="SOT-23 [SMD]"]
  R7 = Resistor [tolerance=±5% resistance=220 package=THT]
  R8 = Resistor [tolerance=±5% resistance=220 package=THT]
  LED2 = smd LED [color="Red (633nm)" package="0805 [SMD]"]
  Q7 = NPN-Transistor [package="SOT-23 [SMD]"]
  R9 = Resistor [tolerance=±5% resistance=220 package=THT]
  R10 = Resistor [tolerance=±5% resistance=220 package=THT]
  LED3 = smd LED [color="Red (633nm)" package="0805 [SMD]"]
  Q8 = NPN-Transistor [package="SOT-23 [SMD]"]
  R11 = Resistor [tolerance=±5% resistance=220 package=THT]
  R12 = Resistor [tolerance=±5% resistance=220 package=THT]
  LED4 = smd LED [color="Red (633nm)" package="0805 [SMD]"]
  S1 = Round Pushbutton
  S2 = Round Pushbutton
  S3 = Round Pushbutton
  S4 = Round Pushbutton

nets:
  GND: U1.COIL2, U2.COIL2, U3.COIL2, U4.COIL2, LED1.cathode, LED2.cathode, LED3.cathode, LED4.cathode, S1.leg1, S2.leg1, S3.leg1, S4.leg1
  Output: U1.NO, U2.NO, U3.NO, U4.NO
  N1: U1.MAIN, D5.cathode
  N2: U1.COIL1, D1.cathode
  N3: U2.MAIN, D6.cathode
  N4: U2.COIL1, D2.cathode
  N5: U3.MAIN, D7.cathode
  N6: U3.COIL1, D3.cathode
  N7: U4.MAIN, D8.cathode
  N8: U4.COIL1, D4.cathode
  N9: D1.anode, Q1.2
  N10: Q1.0, R1.Pin_1
  5V: Q1.1, Q2.1, Q3.1, Q4.1
  N11: D2.anode, Q2.2
  N12: D3.anode, Q3.2
  N13: D4.anode, Q4.2
  N14: Q2.0, R2.Pin_1
  N15: Q3.0, R3.Pin_1
  N16: Q4.0, R4.Pin_1
  cSignalOne: R1.Pin_0
  cSignalTwo: R2.Pin_0
  cSignalThree: R3.Pin_0
  cSignalFor: R4.Pin_0
  Signal 1: D5.anode
  Signal 2: D6.anode
  Signal 3: D7.anode
  Signal 4: D8.anode
  N17: LED1.anode, R6.Pin_0
  N18: Q5.2, R6.Pin_1
  N19: Q5.0, R5.Pin_1
  3.3V: Q5.1, Q6.1, Q7.1, Q8.1
  sLedOne: R5.Pin_0
  N20: Q6.2, R7.Pin_1
  N21: Q6.0, R8.Pin_1
  N22: R7.Pin_0, LED2.anode
  sLedTwo: R8.Pin_0
  N23: Q7.2, R9.Pin_1
  N24: Q7.0, R10.Pin_1
  N25: R9.Pin_0, LED3.anode
  sLedThree: R10.Pin_0
  N26: Q8.2, R11.Pin_1
  N27: Q8.0, R12.Pin_1
  N28: R11.Pin_0, LED4.anode
  sLedFor: R12.Pin_0
  signalOne: S1.leg0
  signalTwo: S2.leg0
  signalThree: S3.leg0
  signalFor: S4.leg0
